// Logisim project e2414860.circ as structural Verilog: 1 circuit, main circuit main
module main (
  input  A1,
  input  A0,
  input  B1,
  input  B0,
  input  S,
  input  O0,
  input  O1,
  input  in_8,
  input  in_9,
  input  in_10,
  input  in_11,
  input  in_12,
  input  in_13,
  input  in_14,
  input  in_15,
  input  in_16,
  output G,
  output E,
  output L,
  output B,
  output L0,
  output L1,
  output L2,
  output L6,
  output L3,
  output L4,
  output L5,
  output L7,
  output N
);

  wire and_1_out, and_2_out, and_3_out, and_4_out, n3_to_8_decoder_74138_1_p4, n3_to_8_decoder_74138_1_p7,
       n3_to_8_decoder_74138_1_p8, n3_to_8_decoder_74138_1_p9, n3_to_8_decoder_74138_1_p10,
       n3_to_8_decoder_74138_1_p11, n3_to_8_decoder_74138_1_p12, n3_to_8_decoder_74138_1_p13,
       n3_to_8_decoder_74138_1_p14, n3_to_8_decoder_74138_2_p4, n3_to_8_decoder_74138_2_p5,
       n3_to_8_decoder_74138_2_p6, n3_to_8_decoder_74138_2_p7, n3_to_8_decoder_74138_2_p8,
       n3_to_8_decoder_74138_2_p9, n3_to_8_decoder_74138_3_p10, n3_to_8_decoder_74138_3_p11,
       n3_to_8_decoder_74138_3_p12, n3_to_8_decoder_74138_3_p13, n3_to_8_decoder_74138_3_p14,
       n3_to_8_decoder_74138_3_p15, n3_to_8_decoder_74138_3_p16, n3_to_8_decoder_74138_3_p17,
       n3_to_8_decoder_74138_3_p18, n3_to_8_decoder_74138_3_p19, n3_to_8_decoder_74138_4_p4,
       n3_to_8_decoder_74138_5_p10, n3_to_8_decoder_74138_5_p11, n3_to_8_decoder_74138_5_p12,
       n3_to_8_decoder_74138_5_p13, n3_to_8_decoder_74138_5_p14, n3_to_8_decoder_74138_5_p15,
       n3_to_8_decoder_74138_5_p16, n4_to_1_mux_x2_74153_1_p9, n4_to_1_mux_x2_74153_1_p10,
       n4_to_1_mux_x2_74153_2_p14, n4_to_1_mux_x2_74153_2_p15, n4_to_1_mux_x2_74153_3_p12,
       n4_to_1_mux_x2_74153_3_p13, n4_to_1_mux_x2_74153_4_p13, n4_to_1_mux_x2_74153_4_p14,
       n4_to_1_mux_x2_74153_5_p13, n4_to_1_mux_x2_74153_6_p15, n4_to_1_mux_x2_74153_7_p11,
       n4_to_1_mux_x2_74153_7_p12, n4_to_1_mux_x2_74153_8_p13, n4_to_1_mux_x2_74153_8_p14,
       n4_to_1_mux_x2_74153_10_p13, n4_to_1_mux_x2_74153_10_p14, not_1_out, not_2_out, not_3_out, not_4_out,
       not_5_out, not_6_out, not_8_out, not_9_out, not_10_out, not_11_out, not_12_out, not_13_out,
       not_14_out, not_15_out, not_16_out, not_17_out, not_18_out, not_19_out, not_20_out, not_21_out,
       not_22_out, not_23_out, not_24_out, not_25_out, not_26_out, not_27_out, not_28_out, not_29_out,
       not_30_out, not_31_out, not_32_out, not_33_out, not_34_out, not_35_out, not_36_out, not_37_out,
       not_38_out, not_39_out, not_40_out, not_41_out, not_42_out, not_43_out, not_44_out, not_45_out,
       not_46_out, not_47_out, not_48_out, not_49_out, not_50_out, not_51_out, not_52_out, not_53_out,
       or_1_out, or_2_out, or_3_out, or_4_out, or_5_out, or_6_out, or_7_out, or_8_out, or_9_out, or_10_out,
       or_11_out, or_12_out, or_15_out, or_16_out, or_17_out, or_18_out, or_19_out, or_20_out, or_21_out,
       or_22_out, or_24_out, or_25_out, or_26_out, or_28_out, or_30_out, or_32_out;

  or or_1 (or_1_out, not_5_out, not_6_out);
  not not_1 (not_1_out, B1);
  not not_2 (not_2_out, B1);
  and and_1 (and_1_out, not_1_out, B0);
  or or_2 (or_2_out, and_1_out, or_5_out);
  not not_3 (not_3_out, A1);
  not not_4 (not_4_out, or_1_out);
  not not_5 (not_5_out, n3_to_8_decoder_74138_1_p8);
  not not_6 (not_6_out, n3_to_8_decoder_74138_1_p7);
  // _3_to_8_decoder__74138 #(.Facing("east")) 3_to_8_decoder_74138_1: pin names not known; wires that end beside it: S, O0, O1, n3_to_8_decoder_74138_1_p4, in_8, in_8, n3_to_8_decoder_74138_1_p7, n3_to_8_decoder_74138_1_p8, n3_to_8_decoder_74138_1_p9, n3_to_8_decoder_74138_1_p10, n3_to_8_decoder_74138_1_p11, n3_to_8_decoder_74138_1_p12, n3_to_8_decoder_74138_1_p13, n3_to_8_decoder_74138_1_p14
  not not_7 (n3_to_8_decoder_74138_1_p4, in_8);
  not not_8 (not_8_out, B0);
  and and_2 (and_2_out, not_2_out, not_8_out);
  not not_9 (not_9_out, B0);
  and and_3 (and_3_out, B1, not_9_out);
  or or_3 (or_3_out, and_2_out, and_3_out);
  or or_4 (or_4_out, and_1_out, and_4_out);
  or or_5 (or_5_out, and_3_out, and_4_out);
  // _3_to_8_decoder__74138 #(.Facing("east")) 3_to_8_decoder_74138_2: pin names not known; wires that end beside it: B0, B1, A0, n3_to_8_decoder_74138_2_p4, n3_to_8_decoder_74138_2_p5, n3_to_8_decoder_74138_2_p6, n3_to_8_decoder_74138_2_p7, n3_to_8_decoder_74138_2_p8, n3_to_8_decoder_74138_2_p9
  // _3_to_8_decoder__74138 #(.Facing("east")) 3_to_8_decoder_74138_3: pin names not known; wires that end beside it: B0, B1, A0, not_3_out, A1, not_4_out, not_4_out, not_4_out, not_4_out, n3_to_8_decoder_74138_3_p10, n3_to_8_decoder_74138_3_p11, n3_to_8_decoder_74138_3_p12, n3_to_8_decoder_74138_3_p13, n3_to_8_decoder_74138_3_p14, n3_to_8_decoder_74138_3_p15, n3_to_8_decoder_74138_3_p16, n3_to_8_decoder_74138_3_p17, n3_to_8_decoder_74138_3_p18, n3_to_8_decoder_74138_3_p19
  not not_10 (not_10_out, n3_to_8_decoder_74138_1_p13);
  not not_11 (not_11_out, n3_to_8_decoder_74138_1_p14);
  and and_4 (and_4_out, B0, B1);
  not not_12 (not_12_out, n3_to_8_decoder_74138_2_p8);
  not not_13 (not_13_out, n3_to_8_decoder_74138_3_p12);
  or or_6 (or_6_out, not_12_out, not_13_out);
  not not_14 (not_14_out, n3_to_8_decoder_74138_3_p13);
  not not_15 (not_15_out, n3_to_8_decoder_74138_3_p16);
  not not_16 (not_16_out, n3_to_8_decoder_74138_1_p12);
  not not_17 (not_17_out, not_16_out);
  not not_18 (not_18_out, in_9);
  not not_19 (not_19_out, in_10);
  not not_20 (not_20_out, not_10_out);
  not not_21 (not_21_out, not_10_out);
  not not_22 (not_22_out, not_10_out);
  not not_23 (not_23_out, not_10_out);
  or or_7 (or_7_out, or_6_out, not_14_out);
  not not_24 (not_24_out, n3_to_8_decoder_74138_3_p17);
  not not_25 (not_25_out, n3_to_8_decoder_74138_3_p18);
  not not_26 (not_26_out, n3_to_8_decoder_74138_1_p9);
  not not_27 (not_27_out, n3_to_8_decoder_74138_1_p10);
  not not_28 (not_28_out, n3_to_8_decoder_74138_1_p11);
  not not_29 (not_29_out, not_11_out);
  not not_30 (not_30_out, not_11_out);
  not not_31 (not_31_out, not_11_out);
  or or_8 (or_8_out, or_7_out, not_15_out);
  not not_32 (not_32_out, n3_to_8_decoder_74138_2_p4);
  not not_33 (not_33_out, n3_to_8_decoder_74138_2_p9);
  not not_34 (not_34_out, n3_to_8_decoder_74138_3_p14);
  not not_35 (not_35_out, n3_to_8_decoder_74138_3_p19);
  or or_9 (or_9_out, not_26_out, not_27_out);
  not not_36 (not_36_out, A1);
  // _4_to_1_MUX__x2___74153 #(.Facing("east")) 4_to_1_mux_x2_74153_1: pin names not known; wires that end beside it: not_18_out, in_9, in_9, in_9, in_9, not_18_out, not_17_out, not_17_out, n4_to_1_mux_x2_74153_1_p9, n4_to_1_mux_x2_74153_1_p10
  // _4_to_1_MUX__x2___74153 #(.Facing("east")) 4_to_1_mux_x2_74153_2: pin names not known; wires that end beside it: in_9, in_9, in_10, in_10, not_19_out, in_10, in_10, in_10, in_10, A0, not_17_out, A1, not_17_out, n4_to_1_mux_x2_74153_2_p14, n4_to_1_mux_x2_74153_2_p15
  // _4_to_1_MUX__x2___74153 #(.Facing("east")) 4_to_1_mux_x2_74153_3: pin names not known; wires that end beside it: not_19_out, and_2_out, in_11, in_11, in_11, and_1_out, and_2_out, A0, not_20_out, A1, not_20_out, n4_to_1_mux_x2_74153_3_p12, n4_to_1_mux_x2_74153_3_p13
  // _4_to_1_MUX__x2___74153 #(.Facing("east")) 4_to_1_mux_x2_74153_4: pin names not known; wires that end beside it: in_11, in_11, and_3_out, and_1_out, and_2_out, in_12, and_4_out, and_3_out, A0, not_21_out, A1, not_21_out, n4_to_1_mux_x2_74153_4_p13, n4_to_1_mux_x2_74153_4_p14
  // _4_to_1_MUX__x2___74153 #(.Facing("east")) 4_to_1_mux_x2_74153_5: pin names not known; wires that end beside it: and_1_out, and_2_out, in_13, and_4_out, and_3_out, and_1_out, in_13, in_13, A0, not_22_out, A1, not_22_out, n4_to_1_mux_x2_74153_5_p13, L5
  // _4_to_1_MUX__x2___74153 #(.Facing("east")) 4_to_1_mux_x2_74153_6: pin names not known; wires that end beside it: and_4_out, and_3_out, in_14, in_14, in_14, and_4_out, in_14, in_14, in_14, in_14, A0, not_23_out, A1, not_23_out, n4_to_1_mux_x2_74153_6_p15, L7
  // _4_to_1_MUX__x2___74153 #(.Facing("east")) 4_to_1_mux_x2_74153_7: pin names not known; wires that end beside it: A0, and_2_out, and_1_out, and_3_out, and_4_out, and_1_out, or_3_out, A1, not_29_out, not_29_out, n4_to_1_mux_x2_74153_7_p11, n4_to_1_mux_x2_74153_7_p12
  // _4_to_1_MUX__x2___74153 #(.Facing("east")) 4_to_1_mux_x2_74153_8: pin names not known; wires that end beside it: or_4_out, and_3_out, and_3_out, and_4_out, and_2_out, and_1_out, and_4_out, in_15, A0, not_30_out, A1, not_30_out, n4_to_1_mux_x2_74153_8_p13, n4_to_1_mux_x2_74153_8_p14
  // _4_to_1_MUX__x2___74153 #(.Facing("east")) 4_to_1_mux_x2_74153_9: pin names not known; wires that end beside it: in_15, and_2_out, or_2_out, or_5_out, and_4_out, in_16, in_16, in_16, in_16, in_16, A0, not_31_out, A0, A1, not_31_out, A1, N
  or or_10 (or_10_out, or_8_out, not_24_out);
  or or_11 (or_11_out, not_32_out, not_33_out);
  or or_12 (or_12_out, not_34_out, not_35_out);
  not not_37 (not_37_out, n3_to_8_decoder_74138_2_p6);
  not not_38 (not_38_out, n3_to_8_decoder_74138_2_p5);
  not not_39 (not_39_out, or_9_out);
  not not_40 (not_40_out, not_28_out);
  // _4_to_1_MUX__x2___74153 #(.Facing("east")) 4_to_1_mux_x2_74153_10: pin names not known; wires that end beside it: A1, A1, A1, A1, not_36_out, not_36_out, not_36_out, not_36_out, not_40_out, A0, not_40_out, A1, n4_to_1_mux_x2_74153_10_p13, n4_to_1_mux_x2_74153_10_p14
  or or_13 (G, or_10_out, not_25_out);
  or or_14 (E, or_11_out, or_12_out);
  or or_15 (or_15_out, not_37_out, not_38_out);
  not not_41 (not_41_out, n3_to_8_decoder_74138_3_p10);
  not not_42 (not_42_out, n3_to_8_decoder_74138_2_p7);
  not not_43 (not_43_out, n3_to_8_decoder_74138_3_p11);
  not not_44 (not_44_out, n3_to_8_decoder_74138_3_p15);
  // _3_to_8_decoder__74138 #(.Facing("east")) 3_to_8_decoder_74138_4: pin names not known; wires that end beside it: B0, B1, A0, n3_to_8_decoder_74138_4_p4
  not not_45 (not_45_out, A1);
  // _3_to_8_decoder__74138 #(.Facing("east")) 3_to_8_decoder_74138_5: pin names not known; wires that end beside it: B0, B1, A0, not_45_out, A1, not_39_out, not_39_out, not_39_out, not_39_out, n3_to_8_decoder_74138_5_p10, n3_to_8_decoder_74138_5_p11, n3_to_8_decoder_74138_5_p12, n3_to_8_decoder_74138_5_p13, n3_to_8_decoder_74138_5_p14, n3_to_8_decoder_74138_5_p15, n3_to_8_decoder_74138_5_p16
  or or_16 (or_16_out, not_42_out, not_41_out);
  or or_17 (or_17_out, not_43_out, not_44_out);
  not not_46 (not_46_out, n3_to_8_decoder_74138_5_p11);
  not not_47 (not_47_out, n3_to_8_decoder_74138_5_p12);
  or or_18 (or_18_out, or_15_out, or_16_out);
  not not_48 (not_48_out, n3_to_8_decoder_74138_4_p4);
  or or_19 (or_19_out, not_48_out, not_49_out);
  not not_49 (not_49_out, n3_to_8_decoder_74138_5_p10);
  or or_20 (or_20_out, not_46_out, not_47_out);
  not not_50 (not_50_out, n3_to_8_decoder_74138_5_p13);
  not not_51 (not_51_out, n3_to_8_decoder_74138_5_p14);
  not not_52 (not_52_out, n3_to_8_decoder_74138_5_p15);
  not not_53 (not_53_out, n3_to_8_decoder_74138_5_p16);
  or or_21 (or_21_out, n4_to_1_mux_x2_74153_10_p14, n4_to_1_mux_x2_74153_1_p9);
  or or_22 (or_22_out, n4_to_1_mux_x2_74153_3_p12, n4_to_1_mux_x2_74153_7_p11);
  or or_23 (L, or_18_out, or_17_out);
  or or_24 (or_24_out, or_19_out, or_20_out);
  or or_25 (or_25_out, not_50_out, not_51_out);
  or or_26 (or_26_out, not_52_out, not_53_out);
  or or_27 (L0, or_21_out, or_22_out);
  or or_28 (or_28_out, n4_to_1_mux_x2_74153_3_p13, n4_to_1_mux_x2_74153_7_p12);
  or or_29 (B, or_24_out, or_30_out);
  or or_30 (or_30_out, or_25_out, or_26_out);
  or or_31 (L1, n4_to_1_mux_x2_74153_10_p13, or_28_out);
  or or_32 (or_32_out, n4_to_1_mux_x2_74153_1_p10, n4_to_1_mux_x2_74153_4_p13);
  or or_33 (L2, or_32_out, n4_to_1_mux_x2_74153_8_p13);
  or or_34 (L6, n4_to_1_mux_x2_74153_2_p15, n4_to_1_mux_x2_74153_6_p15);
  or or_35 (L3, n4_to_1_mux_x2_74153_4_p14, n4_to_1_mux_x2_74153_8_p14);
  or or_36 (L4, n4_to_1_mux_x2_74153_2_p14, n4_to_1_mux_x2_74153_5_p13);

  // Notes on the sheet:
  //   L0
  //   L0
  //   L2
  //   L4
  //   L6
  //   L0
  //   L1
  //   L2
  //   L3
  //   L4
  //   L5
  //   L6
  //   L7
  //   L0
  //   L1
  //   L2
  //   L3
  //   N
  //   L1
  //   L0
endmodule
